// Logisim project aula-03.circ as structural Verilog
module LSR (
  input  Set,
  input  Reset,
  output out_3
);

  wire and_1_out, and_2_out, not_2_out;

  not not_1 (out_3, and_1_out);
  and and_1 (and_1_out, Set, not_2_out);
  not not_2 (not_2_out, and_2_out);
  and and_2 (and_2_out, out_3, Reset);
endmodule

// LD
module LatchD (
  input  Data,
  input  Enable,
  output out_3
);

  wire and_1_out, and_2_out, not_1_out, not_2_out, not_3_out;

  and and_1 (and_1_out, Data, Enable);
  not not_1 (not_1_out, and_1_out);
  not not_2 (not_2_out, and_2_out);
  and and_2 (and_2_out, Enable, not_3_out);
  not not_3 (not_3_out, Data);
  LSR lsr_1 (.Set(not_1_out), .Reset(not_2_out), .out_3(out_3));
endmodule

module flipflop (
  input  Data,
  input  Enable,
  input  Clock,
  output out_4
);

  wire and_1_out, latchd_1_out_3, not_1_out;

  LatchD latchd_1 (.Data(Data), .Enable(and_1_out), .out_3(latchd_1_out_3));
  and and_1 (and_1_out, Enable, Clock);
  not not_1 (not_1_out, Clock);
  LatchD latchd_2 (.Data(latchd_1_out_3), .Enable(not_1_out), .out_3(out_4));
endmodule
